# Fritzing sketch drummer_v2_4 (saved by Fritzing 0.9.2b)
stripboards: 1

parts:
  L1 = Solenoid  # not connected
  L2 = Solenoid  # not connected
  L3 = Solenoid  # not connected
  L4 = Solenoid  # not connected
  Composant1 = Arduino Mega 2560 (Rev3)
  LCD1 = LCD screen
  VCC1 = Battery block 9V
  R5 = Trimmer Potentiometer [maximum_resistance=10kΩ package=THT]
  R6 = Trimmer Potentiometer [maximum_resistance=10kΩ package=THT]
  J2 = Screw terminal - 2 pins [package=THT]  # not connected
  C1 = Ceramic Capacitor [capacitance=100nF voltage=16V package="100 mil [THT, multilayer]"]  # not connected
  C2 = Ceramic Capacitor [capacitance=100nF voltage=16V package="100 mil [THT, multilayer]"]  # not connected
  C3 = Ceramic Capacitor [capacitance=100nF voltage=16V package="100 mil [THT, multilayer]"]  # not connected
  C4 = Ceramic Capacitor [capacitance=100nF voltage=16V package="100 mil [THT, multilayer]"]  # not connected
  Analog_RGB_LED_Strip1 = Analog RGB LED Strip
  U1 = 4RelayModule
  C5 = Ceramic Capacitor [capacitance=100nF voltage=16V package="100 mil [THT, multilayer]"]
  C6 = Ceramic Capacitor [capacitance=100nF voltage=16V package="100 mil [THT, multilayer]"]
  C7 = Ceramic Capacitor [capacitance=100nF voltage=16V package="100 mil [THT, multilayer]"]
  C8 = Ceramic Capacitor [capacitance=100nF voltage=16V package="100 mil [THT, multilayer]"]
  IR1 = TSOP312.., 314.. [package=THT]
  U2 = Voltage Regulator - 5V [package="TO220 [THT]"]  # not connected
  C9 = Ceramic Capacitor [capacitance=100nF voltage=16V package="100 mil [THT, multilayer]"]  # not connected
  C10 = Ceramic Capacitor [capacitance=100nF voltage=16V package="100 mil [THT, multilayer]"]  # not connected
  C11 = Ceramic Capacitor [capacitance=100nF voltage=16V package="100 mil [THT, multilayer]"]  # not connected
  C12 = Ceramic Capacitor [capacitance=100nF voltage=16V package="100 mil [THT, multilayer]"]  # not connected
  VCC2 = Battery
  U3 = 4RelayModule

nets:
  N1: Composant1.D12_PWM, U1.IN1
  N2: Composant1.D11_PWM, U1.IN2
  N3: Composant1.D10_PWM, U1.IN3
  N4: Composant1.D9_PWM, U1.IN4
  5V: Composant1.5V, LCD1.VDD, U1.VCC, IR1.Data
  GND: Composant1.GND, LCD1.VSS, U1.GND, IR1.Vs, VCC2.-
  N5: Composant1.VIN, U1.JD-VCC, VCC2.+
  N6: Composant1.D2_PWM, IR1.GND
  N7: Composant1.D5_PWM, U3.IN3
  N8: Composant1.D6_PWM, U3.IN2
  N9: Composant1.D7_PWM, U3.IN1
  N10: Composant1.D22, LCD1.RS
  N11: Composant1.D23, LCD1.E
  N12: Composant1.D24, LCD1.DB4
  N13: Composant1.D25, LCD1.DB5
  N14: Composant1.D26, LCD1.DB6
  N15: Composant1.D27, LCD1.DB7
  N16: LCD1.V0, R5.wiper
  N17: LCD1.LED+, R6.wiper
  N18: VCC1.-, Analog_RGB_LED_Strip1.12v, C5.0, C6.0, C7.0, C8.0
  N19: VCC1.+, U1.NC1, U1.NC2, U1.NC3, U1.NC4, U3.NC1
  N20: U1.NO1, C8.1
  N21: U1.NO2, C7.1
  N22: U1.NO3, C6.1
  N23: U1.NO4, C5.1

notes:
  12V Motorcycle battery
  2.2K for Mega (4.7K ohm for Leonardo) resistor to Gnd fits instead of POT
  100 ohm to 5V fits instead of POT
  Protected by voltage regulator :
  [+12 volts in]-->[1 ohm, 5 watt resistor]-->[1N5402 diode]-->[1000uF, 25v cap]-->2X [LM7805 ] (to get clean 5V, 1x for arduino, 1x for relay module)
  5m analog led strip (do care with the 12V, some are +12 and other -12 aka ground )
  clean 5V from LM7805
  VS
  1838B
  Notice that relay board has a jumper between "Vcc" and "JD-Vcc". Remove it. For complete optical isolation, connect "Vcc" to Arduino +5 volts but do NOT connect Arduino Ground. Connect your Arduino Digital Output pins to "IN0", "IN1" etc. Connect a separate +5 supply to "JD-Vcc" and board Gnd

custom parts:
  Analog RGB LED Strip: Analog RGB LED strip
  4RelayModule: 4 relay arduino module SONGLE SRD05VDC-SL-C
